# Fritzing sketch sketch (saved by Fritzing 0.9.3b)
breadboards: 1

parts:
  R1 = Resistor [tolerance=±5% resistance=220 package=THT]
  Part1 = Arduino Uno (Rev3)
  LED1 = LED - 5mm [color="Red (633nm)" package="5 mm [THT]"]
  LED2 = LED - 5mm [color="Yellow (592nm)" package="5 mm [THT]"]
  LED3 = LED - 5mm [color="Green (565nm)" package="5 mm [THT]"]
  R2 = Resistor [tolerance=±5% resistance=220 package=THT]
  R3 = Resistor [tolerance=±5% resistance=220 package=THT]
  J1 = Piezo Speaker

nets:
  N1: R1.Pin_0, LED1.cathode
  N2: R1.Pin_1, Part1.GND, R2.Pin_1, R3.Pin_1, J1.pin2
  N3: Part1.D11_PWM/MOSI, LED3.anode
  N4: Part1.D12/MISO, LED2.anode
  N5: Part1.D13/SCK, LED1.anode
  N6: Part1.D6_PWM, J1.pin1
  N7: LED2.cathode, R2.Pin_0
  N8: LED3.cathode, R3.Pin_0
