# Fritzing sketch sketch (saved by Fritzing 0.9.3b)
breadboards: 1

parts:
  R1 = Resistor [tolerance=±5% resistance=10k package=THT]
  S1 = Pushbutton [package="[THT]"]
  LED1 = LED - 5mm [color="Red (633nm)" package="5 mm [THT]"]
  Part1 = Arduino Uno (Rev3)
  R2 = Resistor [tolerance=±5% resistance=220 package=THT]

nets (from the schematic view):
  N1: R1.Pin_0, S1.Pin_1, S1.Pin_2, Part1.D2
  N2: R1.Pin_1, Part1.GND, R2.Pin_1
  N3: S1.Pin_3, S1.Pin_4, Part1.5V
  N4: LED1.cathode, R2.Pin_0
  N5: LED1.anode, Part1.D13/SCK
